# Fritzing sketch Fastlamp (saved by Fritzing 0.9.3b)
circuit board: 8cm x 2.9cm
breadboards: 1

parts:
  GND = female pin header, 3 pins [form="♀ (female)"]
  1000uF = Capacitor Polarized [package=cpol-radial-1000uf-25v]
  WeMos_D1_Mini1 = WeMos D1 Mini
  74X245N = IC, DIP package, 20 pins [chip_label=74X245N]

nets:
  N1: GND.pin1, 1000uF.-, WeMos_D1_Mini1.G, 74X245N.pin1, 74X245N.pin10, 74X245N.pin19
  N2: GND.pin2, 1000uF.+, WeMos_D1_Mini1.5V, 74X245N.pin20
  N3: GND.pin3, 74X245N.pin9
  N4: WeMos_D1_Mini1.D5, 74X245N.pin11

notes:
  5v
  DI
  GND
  FastLamp
  -
  D5
  v1.0.0 - @kokuma
